// Logisim project control.circ as structural Verilog: 1 circuit, main circuit control_unit
// control\n unit
module control_unit (
  input  lsb_bit,
  input  counter32,
  input  start,
  input  clock,
  output load_product,
  output load_multiplier,
  output shift,
  output enable_out,
  output increment,
  output clear
);

  wire and_6_out, and_7_out, and_8_out, and_10_out, not_1_out, not_2_out, not_3_out, not_4_out, not_5_out,
       not_6_out, not_7_out, not_8_out, not_9_out, not_10_out, not_11_out, not_12_out, not_13_out,
       not_14_out, not_15_out, not_16_out, not_17_out, not_18_out, not_19_out, or_1_out, or_2_out, xor_1_out;
  wire [2:0] or_3_out, register_1_q;

  Register #(.width(3)) register_1 (.D(or_3_out), .Q(register_1_q), .clk(clock));  // open: en, clr
  not not_1 (not_1_out, register_1_q[2]);
  not not_2 (not_2_out, register_1_q[0]);
  not not_3 (not_3_out, register_1_q[1]);
  not not_4 (not_4_out, register_1_q[1]);
  not not_5 (not_5_out, register_1_q[0]);
  not not_6 (not_6_out, register_1_q[2]);
  not not_7 (not_7_out, register_1_q[1]);
  not not_8 (not_8_out, register_1_q[2]);
  or or_1 (or_1_out, lsb_bit, counter32);
  not not_9 (not_9_out, register_1_q[0]);
  not not_10 (not_10_out, register_1_q[2]);
  not not_11 (not_11_out, register_1_q[0]);
  not not_12 (not_12_out, register_1_q[1]);
  not not_13 (not_13_out, register_1_q[2]);
  not not_14 (not_14_out, counter32);
  not not_15 (not_15_out, register_1_q[2]);
  not not_16 (not_16_out, register_1_q[0]);
  not not_17 (not_17_out, register_1_q[1]);
  not not_18 (not_18_out, register_1_q[2]);
  not not_19 (not_19_out, lsb_bit);
  and and_1 (load_product, register_1_q[0], register_1_q[1], not_1_out);
  and and_2 (shift, not_2_out, not_3_out, register_1_q[2]);
  and and_3 (enable_out, register_1_q[0], not_4_out, register_1_q[2]);
  and and_4 (increment, not_5_out, register_1_q[1], not_6_out);
  and and_5 (clear, register_1_q[0], not_7_out, not_8_out);
  and and_6 (and_6_out, or_1_out, not_9_out, register_1_q[1], not_10_out);
  and and_7 (and_7_out, start, not_11_out, not_12_out, not_13_out);
  and and_8 (and_8_out, lsb_bit, not_14_out, not_15_out, register_1_q[1], not_16_out);
  xor xor_1 (xor_1_out, register_1_q[2], register_1_q[0]);
  and and_9 (or_3_out[2], register_1_q[1], not_18_out, or_2_out);
  or or_2 (or_2_out, not_19_out, counter32, register_1_q[0]);
  or or_3 (or_3_out[0], and_6_out, and_7_out);
  or or_4 (or_3_out[1], and_8_out, and_10_out);
  and and_10 (and_10_out, xor_1_out, not_17_out);

  assign load_multiplier = clear;

  // Notes on the sheet:
  //   n2
  //   n0
  //   n1
endmodule
