// Logisim project datapath.circ as structural Verilog: 2 circuits, main circuit datapath
module datapath (
  input  [31:0] Multiplier_input,
  input  [31:0] Multiplicand_input,
  input  load_product,
  input  load_multiplier,
  input  shift,
  input  enable_out,
  input  increment,
  input  clear,
  input  clock,
  output lsb_bit,
  output [31:0] \output ,
  output counter32
);

  wire [5:0] counter_1_q;
  wire [31:0] adder_1_out, n64bit_shifter_1_first_half_2;
  wire [31:1] n64bit_shifter_1_second_half_2;

  Counter #(.width(6), .max('h3f)) counter_1 (
    .count(increment), .Q(counter_1_q), .clk(clock), .clr(clear));  // open: load, D, carry
  Adder #(.width(32)) adder_1 (
    .a(Multiplicand_input), .b(n64bit_shifter_1_first_half_2), .out(adder_1_out));  // open: cin, cout
  _64bit_shifter u_64bit_shifter_1 (
    .second_half(Multiplier_input), .first_half(adder_1_out), .load_first(load_product),
    .load_second(load_multiplier), .shift(shift), .clock(clock),
    .second_half_2({n64bit_shifter_1_second_half_2, lsb_bit}), .first_half_2(n64bit_shifter_1_first_half_2));
  Register #(.width(32)) register_1 (
    .D({n64bit_shifter_1_second_half_2, lsb_bit}), .en(enable_out), .Q(\output ), .clk(clock), .clr(clear));
  Comparator #(.width(6), .mode("unsigned")) comparator_1 (
    .a(6'b011111), .b(counter_1_q), .lt(counter32));  // open: gt, eq
endmodule

// shifter
module _64bit_shifter (
  input  [31:0] second_half,
  input  [31:0] first_half,
  input  load_first,
  input  load_second,
  input  shift,
  input  clock,
  output [31:0] second_half_2,
  output [31:0] first_half_2
);

  wire shift_register_1_out;

  Shift_Register #(.length(32)) shift_register_1 (
    .shift(shift), .in(1'b0), .clk(clock), .out(shift_register_1_out), .load(load_first),
    .d0(first_half[31]), .q0(first_half_2[31]), .d1(first_half[30]), .q1(first_half_2[30]),
    .d2(first_half[29]), .q2(first_half_2[29]), .d3(first_half[28]), .q3(first_half_2[28]),
    .d4(first_half[27]), .q4(first_half_2[27]), .d5(first_half[26]), .q5(first_half_2[26]),
    .d6(first_half[25]), .q6(first_half_2[25]), .d7(first_half[24]), .q7(first_half_2[24]),
    .d8(first_half[23]), .q8(first_half_2[23]), .d9(first_half[22]), .q9(first_half_2[22]),
    .d10(first_half[21]), .q10(first_half_2[21]), .d11(first_half[20]), .q11(first_half_2[20]),
    .d12(first_half[19]), .q12(first_half_2[19]), .d13(first_half[18]), .q13(first_half_2[18]),
    .d14(first_half[17]), .q14(first_half_2[17]), .d15(first_half[16]), .q15(first_half_2[16]),
    .d16(first_half[15]), .q16(first_half_2[15]), .d17(first_half[14]), .q17(first_half_2[14]),
    .d18(first_half[13]), .q18(first_half_2[13]), .d19(first_half[12]), .q19(first_half_2[12]),
    .d20(first_half[11]), .q20(first_half_2[11]), .d21(first_half[10]), .q21(first_half_2[10]),
    .d22(first_half[9]), .q22(first_half_2[9]), .d23(first_half[8]), .q23(first_half_2[8]),
    .d24(first_half[7]), .q24(first_half_2[7]), .d25(first_half[6]), .q25(first_half_2[6]),
    .d26(first_half[5]), .q26(first_half_2[5]), .d27(first_half[4]), .q27(first_half_2[4]),
    .d28(first_half[3]), .q28(first_half_2[3]), .d29(first_half[2]), .q29(first_half_2[2]),
    .d30(first_half[1]), .q30(first_half_2[1]), .d31(first_half[0]), .q31(first_half_2[0]));  // open: clr
  Shift_Register #(.length(32)) shift_register_2 (
    .shift(shift), .in(shift_register_1_out), .clk(clock), .load(load_second), .d0(second_half[31]),
    .q0(second_half_2[31]), .d1(second_half[30]), .q1(second_half_2[30]), .d2(second_half[29]),
    .q2(second_half_2[29]), .d3(second_half[28]), .q3(second_half_2[28]), .d4(second_half[27]),
    .q4(second_half_2[27]), .d5(second_half[26]), .q5(second_half_2[26]), .d6(second_half[25]),
    .q6(second_half_2[25]), .d7(second_half[24]), .q7(second_half_2[24]), .d8(second_half[23]),
    .q8(second_half_2[23]), .d9(second_half[22]), .q9(second_half_2[22]), .d10(second_half[21]),
    .q10(second_half_2[21]), .d11(second_half[20]), .q11(second_half_2[20]), .d12(second_half[19]),
    .q12(second_half_2[19]), .d13(second_half[18]), .q13(second_half_2[18]), .d14(second_half[17]),
    .q14(second_half_2[17]), .d15(second_half[16]), .q15(second_half_2[16]), .d16(second_half[15]),
    .q16(second_half_2[15]), .d17(second_half[14]), .q17(second_half_2[14]), .d18(second_half[13]),
    .q18(second_half_2[13]), .d19(second_half[12]), .q19(second_half_2[12]), .d20(second_half[11]),
    .q20(second_half_2[11]), .d21(second_half[10]), .q21(second_half_2[10]), .d22(second_half[9]),
    .q22(second_half_2[9]), .d23(second_half[8]), .q23(second_half_2[8]), .d24(second_half[7]),
    .q24(second_half_2[7]), .d25(second_half[6]), .q25(second_half_2[6]), .d26(second_half[5]),
    .q26(second_half_2[5]), .d27(second_half[4]), .q27(second_half_2[4]), .d28(second_half[3]),
    .q28(second_half_2[3]), .d29(second_half[2]), .q29(second_half_2[2]), .d30(second_half[1]),
    .q30(second_half_2[1]), .d31(second_half[0]), .q31(second_half_2[0]));  // open: out, clr
endmodule
