// Logisim project mult32.circ as structural Verilog: 1 circuit, main circuit main
module main (
  input  [31:0] in_1,
  input  [31:0] in_2,
  output [31:0] \output 
);

  wire clock_1_out, control_unit_1_clear, control_unit_1_enable_out, control_unit_1_increment,
       control_unit_1_load_multiplier, control_unit_1_load_product, control_unit_1_shift,
       datapath_1_counter32, datapath_1_lsb_bit, start_out;

  Button start (.out(start_out));
  Clock clock_1 (.out(clock_1_out));
  control_unit control_unit_1 (
    .lsb_bit(datapath_1_lsb_bit), .counter32(datapath_1_counter32), .start(start_out), .clock(clock_1_out),
    .load_product(control_unit_1_load_product), .load_multiplier(control_unit_1_load_multiplier),
    .shift(control_unit_1_shift), .enable_out(control_unit_1_enable_out),
    .increment(control_unit_1_increment), .clear(control_unit_1_clear));
  datapath datapath_1 (
    .Multiplier_input(in_1), .Multiplicand_input(in_2), .load_product(control_unit_1_load_product),
    .load_multiplier(control_unit_1_load_multiplier), .shift(control_unit_1_shift),
    .enable_out(control_unit_1_enable_out), .increment(control_unit_1_increment),
    .clear(control_unit_1_clear), .clock(clock_1_out), .lsb_bit(datapath_1_lsb_bit), .\output (\output ),
    .counter32(datapath_1_counter32));
endmodule
